# Fritzing sketch prog-timer-test-setup (saved by Fritzing 0.9.4)

parts:
  KT1 = Programmable Timer Module - Lite Version [part_number=KT0003 package=THT]
  J1 = Piezo Speaker

nets:
  N1: KT1.OUTPUT, J1.pin1
  N2: KT1.VCC, J1.pin2

notes:
  Input from +5V DC Power Supply
  +
  -

custom parts:
  Programmable Timer Module - Lite Version: Programmable Timer Module - Single channel
